// Logisim project Microprocessor.circ as structural Verilog: 4 circuits, main circuit RegisterFile
module RegisterFile (
  input  WE,
  input  [3:0] WA,
  input  [15:0] INP,
  input  CLK,
  input  [3:0] RA1,
  input  [3:0] RA2,
  output [15:0] OUT2,
  output [15:0] OUT1
);

  wire decoder_1_out0, decoder_1_out1, decoder_1_out2, decoder_1_out3, decoder_1_out4, decoder_1_out5,
       decoder_1_out6, decoder_1_out7, decoder_1_out8, decoder_1_out9, decoder_1_out10, decoder_1_out11,
       decoder_1_out12, decoder_1_out13, decoder_1_out14, decoder_1_out15;
  wire [15:0] register_1_q, register_2_q, register_3_q, register_4_q, register_5_q, register_6_q,
       register_7_q, register_8_q, register_9_q, register_10_q, register_11_q, register_12_q, register_13_q,
       register_14_q, register_15_q, register_16_q;

  Register #(.width(16), .Select("low")) register_1 (
    .D(INP), .en(decoder_1_out3), .Q(register_1_q), .clk(CLK));  // open: clr
  Register #(.width(16), .Select("low")) register_2 (
    .D(INP), .en(decoder_1_out2), .Q(register_2_q), .clk(CLK));  // open: clr
  Register #(.width(16), .Select("low")) register_3 (
    .D(INP), .en(decoder_1_out1), .Q(register_3_q), .clk(CLK));  // open: clr
  Register #(.width(16), .Select("low")) register_4 (
    .D(INP), .en(decoder_1_out0), .Q(register_4_q), .clk(CLK));  // open: clr
  Decoder #(.select(4)) decoder_1 (
    .out0(decoder_1_out0), .out1(decoder_1_out1), .out2(decoder_1_out2), .out3(decoder_1_out3),
    .out4(decoder_1_out4), .out5(decoder_1_out5), .out6(decoder_1_out6), .out7(decoder_1_out7),
    .out8(decoder_1_out8), .out9(decoder_1_out9), .out10(decoder_1_out10), .out11(decoder_1_out11),
    .out12(decoder_1_out12), .out13(decoder_1_out13), .out14(decoder_1_out14), .out15(decoder_1_out15),
    .sel(WA), .en(WE));
  Register #(.width(16), .Select("low")) register_5 (
    .D(INP), .en(decoder_1_out7), .Q(register_5_q), .clk(CLK));  // open: clr
  Register #(.width(16), .Select("low")) register_6 (
    .D(INP), .en(decoder_1_out6), .Q(register_6_q), .clk(CLK));  // open: clr
  Register #(.width(16), .Select("low")) register_7 (
    .D(INP), .en(decoder_1_out5), .Q(register_7_q), .clk(CLK));  // open: clr
  Register #(.width(16), .Select("low")) register_8 (
    .D(INP), .en(decoder_1_out4), .Q(register_8_q), .clk(CLK));  // open: clr
  Register #(.width(16), .Select("low")) register_9 (
    .D(INP), .en(decoder_1_out11), .Q(register_9_q), .clk(CLK));  // open: clr
  Register #(.width(16), .Select("low")) register_10 (
    .D(INP), .en(decoder_1_out10), .Q(register_10_q), .clk(CLK));  // open: clr
  Register #(.width(16), .Select("low")) register_11 (
    .D(INP), .en(decoder_1_out9), .Q(register_11_q), .clk(CLK));  // open: clr
  Register #(.width(16), .Select("low")) register_12 (
    .D(INP), .en(decoder_1_out8), .Q(register_12_q), .clk(CLK));  // open: clr
  Register #(.width(16), .Select("low")) register_13 (
    .D(INP), .en(decoder_1_out15), .Q(register_13_q), .clk(CLK));  // open: clr
  Register #(.width(16), .Select("low")) register_14 (
    .D(INP), .en(decoder_1_out14), .Q(register_14_q), .clk(CLK));  // open: clr
  Register #(.width(16), .Select("low")) register_15 (
    .D(INP), .en(decoder_1_out13), .Q(register_15_q), .clk(CLK));  // open: clr
  Register #(.width(16), .Select("low")) register_16 (
    .D(INP), .en(decoder_1_out12), .Q(register_16_q), .clk(CLK));  // open: clr
  Multiplexer #(.select(4), .width(16), .enable("false")) multiplexer_1 (
    .in0(register_4_q), .in1(register_3_q), .in2(register_2_q), .in3(register_1_q), .in4(register_8_q),
    .in5(register_7_q), .in6(register_6_q), .in7(register_5_q), .in8(register_12_q), .in9(register_11_q),
    .in10(register_10_q), .in11(register_9_q), .in12(register_16_q), .in13(register_15_q),
    .in14(register_14_q), .in15(register_13_q), .out(OUT1), .sel(RA1));
  Multiplexer #(.select(4), .width(16), .enable("false")) multiplexer_2 (
    .in0(register_4_q), .in1(register_3_q), .in2(register_2_q), .in3(register_1_q), .in4(register_8_q),
    .in5(register_7_q), .in6(register_6_q), .in7(register_5_q), .in8(register_12_q), .in9(register_11_q),
    .in10(register_10_q), .in11(register_9_q), .in12(register_16_q), .in13(register_15_q),
    .in14(register_14_q), .in15(register_13_q), .out(OUT2), .sel(RA2));
endmodule

module ALU (
  input  [15:0] in_1,
  input  [15:0] in_2,
  input  [2:0] in_3,
  output [15:0] out_4,
  output out_5,
  output out_6,
  output out_7
);

  wire [15:0] adder_1_out, and_1_out, multiplier_1_out, negator_1_out, not_1_out, or_1_out, subtractor_1_out;

  assign not_1_out = ~in_1;  // NOT_Gate not_1, 16 bits wide
  assign and_1_out = in_1 & in_2;  // AND_Gate and_1, 16 bits wide
  assign or_1_out = in_1 | in_2;  // OR_Gate or_1, 16 bits wide
  Adder #(.width(16)) adder_1 (.a(in_1), .b(in_2), .out(adder_1_out));  // open: cin, cout
  Subtractor #(.width(16)) subtractor_1 (.a(in_1), .b(in_2), .out(subtractor_1_out));  // open: bin, bout
  Negator #(.width(16)) negator_1 (.in(in_1), .out(negator_1_out));
  Multiplier #(.width(16)) multiplier_1 (.a(in_1), .b(in_2), .out(multiplier_1_out));  // open: cin, cout
  Comparator #(.width(16)) comparator_1 (.a(in_1), .b(in_2), .gt(out_5), .eq(out_6), .lt(out_7));
  Multiplexer #(.select(3), .width(16), .enable("false")) multiplexer_1 (
    .in0(not_1_out), .in1(and_1_out), .in2(or_1_out), .in3(adder_1_out), .in4(subtractor_1_out),
    .in5(negator_1_out), .in6(multiplier_1_out), .out(out_4), .sel(in_3));  // open: in7

  // Notes on the sheet:
  //   $$$
endmodule

module Program_Counter (
  input  in_1,
  input  in_2,
  input  [15:0] in_3,
  input  in_4,
  output [15:0] out_5
);

  wire [15:0] adder_1_out, multiplexer_1_out;

  Adder #(.width(16)) adder_1 (.a(out_5), .b(16'h1), .out(adder_1_out));  // open: cin, cout
  Multiplexer #(.width(16), .enable("false")) multiplexer_1 (
    .in0(adder_1_out), .in1(in_3), .out(multiplexer_1_out));  // open: sel
  Register #(.width(16), .Select("low")) register_1 (
    .D(multiplexer_1_out), .en(in_1), .Q(out_5), .clk(in_4), .clr(in_2));
endmodule

module main (
  input  [2:0] in_1,
  output [15:0] out_2
);

  wire [15:0] program_counter_1_out_5, ram_1_data, registerfile_1_out1, registerfile_1_out2;

  Program_Counter program_counter_1 (.out_5(program_counter_1_out_5));  // open: in_1, in_4, in_2, in_3
  RAM #(.addrWidth(16), .dataWidth(16), .Select("low")) ram_1 (
    .addr(program_counter_1_out_5), .data(ram_1_data));  // open: sel, clk, ld, clr
  RegisterFile registerfile_1 (
    .WA(ram_1_data[12:9]), .RA1(ram_1_data[8:5]), .RA2(ram_1_data[12:9]), .OUT2(registerfile_1_out2),
    .OUT1(registerfile_1_out1));  // open: INP, CLK, WE
  // Probe on registerfile_1_out1
  ALU alu_1 (
    .in_1(registerfile_1_out1), .in_2(registerfile_1_out2), .out_4(out_2), .in_3(in_1));  // open: out_5, out_6, out_7
endmodule
